# Fritzing sketch PowerMeter TSL257 and SD (saved by Fritzing 0.6.5b)
breadboards: 1

parts:
  Arduino1 = Arduino
  R1 = Resistor [tolerance=±5% resistance=220 package=THT]
  U1 = IC, SIP package, 3 pins [chip_label=TSL spacing=300mil part_number=TSL257-LF]
  U2 = IC, SIP package, 6 pins [chip_label=SD spacing=300mil part_number="SD-module DFrobot"]

nets:
  N1: Arduino1.GND, R1.Pin_1, U1.pin1, U2.pin5
  N2: Arduino1.D13, U2.pin2
  N3: Arduino1.D12, U2.pin1
  N4: Arduino1.D11, U2.pin4
  N5: Arduino1.D10, U2.pin3
  N6: Arduino1.D3, R1.Pin_0, U1.pin3
  N7: Arduino1.+5V, U1.pin2, U2.pin6

notes:
  TSL and SD parts have problems with PIN associations. Check carefully.
